# Fritzing sketch Wire Diagram Src File (saved by Fritzing 0.9.3b)
breadboards: 1

parts:
  Part1 = Arduino Uno (Rev3) - ICSP
  HC-SR04_Sensor_1 = HC-SR04 Ultrasonic Distance Sensor
  HC-SR04_Sensor_2 = HC-SR04 Ultrasonic Distance Sensor
  DHT2 = DHT11 Humitidy and Temperature Sensor (3 pins)
  Sensor1 = Gas Sensor Breakout Board
  microSD1 = MicroSD Card Module
  RTC1 = DS3231 AT24C32 Real Time Clock
  VCC1 = 4 x AAA Battery Mount

nets:
  N1: Part1.A0, Sensor1.AOUT
  N2: Part1.A4/SDA, RTC1.SDA
  N3: Part1.A5/SCL, RTC1.SCL
  N4: Part1.D10_PWM/SS, microSD1.CS
  N5: Part1.D11_PWM/MOSI, microSD1.MOSI
  N6: Part1.D12/MISO, microSD1.MISO
  N7: Part1.D13/SCK, microSD1.SCK
  GND: Part1.GND, HC-SR04_Sensor_1.GND, HC-SR04_Sensor_2.GND, DHT2.Gnd, Sensor1.GND, microSD1.GND, RTC1.GND, VCC1.-
  N8: Part1.D2, RTC1.SQW
  N9: Part1.D3_PWM, DHT2.Signal
  N10: Part1.D4, HC-SR04_Sensor_2.ECHO
  N11: Part1.D5_PWM, HC-SR04_Sensor_2.TRIG
  N12: Part1.D6_PWM, HC-SR04_Sensor_1.ECHO
  N13: Part1.D7, HC-SR04_Sensor_1.TRIG
  VCC: Part1.5V, HC-SR04_Sensor_1.VCC, HC-SR04_Sensor_2.VCC, DHT2.Plus, Sensor1.5V, microSD1.VCC, RTC1.VCC, VCC1.+

custom parts:
  DHT11 Humitidy and Temperature Sensor (3 pins): DHT11 Humidity and Temperature Sensor (3 pins).
  Gas Sensor Breakout Board: Gas sensor breakout board. Input voltage is 5V. Sensor output is available in analog and digital.
  MicroSD Card Module: A common microSD card module.
  DS3231 AT24C32 Real Time Clock: Real-time clock basedo on chip DS3231, plus memory chip AT24C32 (32 Kb storage capacity). On-chip temperature sensor with an accuracy of ±3 ℃, I2C bus interface maximum speed: 400 kHz. Operating voltage: 3.3 V to 5.5 V with battery backup capabilities.
